# Fritzing sketch ble_switch (saved by Fritzing 0.9.3b)

parts:
  U1 = RELAY-SOLIDSTATE [package=relay-s108t02]
  U2 = RELAY-SOLIDSTATE [package=relay-s108t02]
  U3 = RELAY-SOLIDSTATE [package=relay-s108t02]
  Power_plug1 = Power plug
  Part1 = Arduino Pro Mini v13
  J1 = Power Jack [package=power_jack_pth_lock]
  Part4 = Bluetooth Mate Silver
  LED2 = LEDs [package=led10mm]
  LED1 = LEDs [package=led10mm]
  LED3 = LEDs [package=led10mm]

nets:
  N1: U1.T1, U2.T1, U3.T1, J1.GND
  N2: U1.T2, LED1.C
  N3: U1.+, Part1.D9_PWM
  GND: U1.-, Power_plug1.GND, Part1.GND, Part4.GND
  N4: U2.T2, LED2.C
  N5: U2.+, Part1.D4
  N6: U2.-, U3.-
  N7: U3.T2, LED3.C
  N8: U3.+, Part1.D2
  N9: Power_plug1.VCC, Part1.RAW
  VCC: Part1.VCC, Part4.VCC
  N10: Part1.D11_PWM/MOSI, Part4.TX_5V
  N11: Part1.D10_PWM/SS, Part4.RX_5V
  N12: J1.GNDBREAK, LED2.A, LED1.A, LED3.A
